# Fritzing sketch schematic (saved by Fritzing 0.9.2b)

parts:
  Part1 = Arduino Uno (Rev3) - ICSP
  U1 = POT [package=pot_mammoth]
  LED1 = 7-SEGMENT-4DIGIT-YOUNGSUN [package=7-segment-4digit-youngsun]
  R1 = Resistor [tolerance=±5% resistance=1k package=THT]
  ANT1 = Antenna  # not connected
  R2 = Resistor [tolerance=±5% resistance=1k package=THT]
  R3 = Resistor [tolerance=±5% resistance=1k package=THT]
  R4 = Resistor [tolerance=±5% resistance=1k package=THT]

nets:
  N1: Part1.A0, U1.S
  N2: Part1.D8, LED1.E
  N3: Part1.D9_PWM, LED1.D
  N4: Part1.D10_PWM/SS, LED1.DIG2
  N5: Part1.D11_PWM/MOSI, LED1.C
  N6: Part1.D12/MISO, LED1.DIG3
  N7: Part1.D13/SCK, LED1.COL-A
  N8: Part1.D2, R1.Pin_0
  N9: Part1.D3_PWM, R2.Pin_0
  N10: Part1.D4, R3.Pin_0
  N11: Part1.D5_PWM, R4.Pin_0
  N12: Part1.D6_PWM, LED1.A
  N13: Part1.D7, LED1.APOS-A
  N14: Part1.5V, U1.E
  N15: Part1.GND, U1.A
  N16: LED1.DP, R4.Pin_1
  N17: LED1.F, R3.Pin_1
  N18: LED1.COL-C, R2.Pin_1
  N19: LED1.G, R1.Pin_1

notes:
  Control frequency
  Better range
  Audio input
  Display Frequency
